// Logisim project 12bit_CPU.circ as structural Verilog: 19 circuits, main circuit Layout
module Layout (
  input  [1:0] in_1,
  input  [11:0] in_2,
  input  [11:0] in_3,
  input  [11:0] in_4,
  input  [11:0] in_5,
  output BS_E,
  output BS_L,
  output ALU_E,
  output [11:0] out_9,
  output ALU_L,
  output OUT_L,
  output IN_E,
  output out_13,
  output B_E,
  output out_15,
  output B_L,
  output A_E,
  output A_L,
  output IR_E,
  output [11:0] out_20,
  output IR_L,
  output SP_I,
  output SP_D,
  output SP_E,
  output SP_L,
  output RAM_E,
  output RAM_L,
  output MDR_E,
  output [11:0] out_29,
  output MDR_L,
  output MAR_E,
  output MAR_L,
  output PC_I,
  output PC_E,
  output [3:0] out_35,
  output [3:0] out_36,
  output PC_L,
  output RESET,
  output STOP,
  output START,
  output [11:0] out_41,
  output [11:0] out_42,
  output [11:0] out_43,
  output [11:0] out_44
);

  wire button_1_out, button_2_out, button_3_out, button_4_out, button_5_out, button_6_out, button_7_out,
       button_8_out, button_9_out, button_10_out, button_11_out, CND_out_6, controlled_buffer_1_out,
       controlled_buffer_2_out, not_1_out, or_1_out, start_stop_1_out_3;
  wire [3:0] _4_BIT_MOD_out_5, decoding_1_out_3, PC_out_6, PC_out_6_2, rom_1_data, undriven;
  wire [5:0] decoding_1_ir;
  wire [7:0] ir_reg_1_out_5, mar_1_out_4;
  wire [11:0] buffer_1_out, MDR_out_5;

  ROM #(.addrWidth(12), .dataWidth(32)) rom_1 (
    .addr({ir_reg_1_out_5, _4_BIT_MOD_out_5}),
    .data({BS_E, BS_L, ALU_E, ALU_L, OUT_L, IN_E, B_E, B_L, A_E, A_L, IR_E, IR_L, SP_I, SP_D, SP_E, SP_L, RAM_E, RAM_L, MDR_E, MDR_L, MAR_E, MAR_L, PC_I, PC_E, PC_L, RESET, STOP, START, rom_1_data}),
    .sel(1'b1));
  assign controlled_buffer_1_out = not_1_out ? MDR_E : 1'bz;  // Controlled_Buffer controlled_buffer_1
  assign controlled_buffer_2_out = not_1_out ? PC_L : 1'bz;  // Controlled_Buffer controlled_buffer_2
  not not_1 (not_1_out, rom_1_data[1]);
  assign buffer_1_out = {undriven, PC_out_6_2, PC_out_6};  // Buffer buffer_1, 12 bits wide
  assign buffer_1_out = out_29;  // Buffer buffer_2, 12 bits wide
  RAM_part #(.dataWidth(12), .bus("separate")) ram_1 (
    .addr(mar_1_out_4), .din(buffer_1_out), .data(out_29), .str(RAM_L), .sel(1'b1), .clk(RAM_L), .ld(RAM_E),
    .clr(1'b0));
  Button button_1 (.out(button_1_out));
  PC PC (
    .out_6({PC_out_6_2, PC_out_6}), .I(PC_I), .in_2({PC_out_6_2, PC_out_6}), .in_3(PC_E),
    .in_4(controlled_buffer_2_out), .in_5(button_10_out));
  MAR mar_1 (.in_1({PC_out_6_2, PC_out_6}), .in_2(MAR_L), .in_3(MAR_E), .out_4(mar_1_out_4));
  Button button_2 (.out(button_2_out));
  Button button_3 (.out(button_3_out));
  CND CND (
    .in_1(out_15), .in_2(out_13), .in_3(rom_1_data[3]), .in_4(rom_1_data[2]), .in_5(rom_1_data[1]),
    .out_6(CND_out_6));
  IN_PORT in_port_1 (
    .in_1(in_3), .in_2(button_4_out), .in_3(in_5), .in_4(button_3_out), .in_5(in_4), .in_6(in_2),
    .in_7(IN_E), .in_8(decoding_1_out_3), .in_9(button_2_out), .in_10(button_1_out), .out_11(out_29),
    .out_12(out_35));
  Button button_4 (.out(button_4_out));
  SP SP (.I(SP_I), .out_7({PC_out_6_2, PC_out_6}), .E(SP_E), .L(SP_L), .D(SP_D), .START(button_10_out));  // open: in_3
  buf buffer_3 (controlled_buffer_2_out, CND_out_6);
  assign {PC_out_6_2, PC_out_6} = MDR_out_5[7:0];  // Buffer buffer_4, 8 bits wide
  buf buffer_5 (controlled_buffer_1_out, CND_out_6);
  reg_12bit MDR (.in_1(out_29), .L(MDR_L), .E(controlled_buffer_1_out), .out_5(MDR_out_5));  // open: out_4
  Button button_5 (.out(button_5_out));
  Button button_6 (.out(button_6_out));
  Button button_7 (.out(button_7_out));
  DECODING decoding_1 (.IR(decoding_1_ir), .out_3(decoding_1_out_3), .MDR(MDR_out_5));
  OUT_PORT out_port_1 (
    .in_1(out_29), .in_2(button_8_out), .in_3(button_7_out), .in_4(OUT_L), .in_5(decoding_1_out_3),
    .in_6(button_6_out), .in_7(button_5_out), .out_8(out_43), .out_9(out_41), .out_10(out_36),
    .out_11(out_44), .out_12(out_42));
  Button button_8 (.out(button_8_out));
  SHIFTER shifter_1 (.in_1(out_29), .in_3(MDR_out_5), .out_5(out_29), .in_4(BS_E), .in_2(BS_L));
  reg_12bit B (.in_1(out_29), .L(B_L), .E(B_E), .out_5(out_29), .out_4(out_20));
  reg_12bit A (.in_1(out_29), .L(A_L), .E(A_E), .out_5(out_29), .out_4(out_9));
  Button button_9 (.out(button_9_out));
  IR_REG ir_reg_1 (
    .in_1({in_1, decoding_1_ir}), .in_2(IR_L), .in_3(button_10_out), .out_5(ir_reg_1_out_5), .in_4(IR_E));
  MOD_COUNTER _4_BIT_MOD (
    .in_3(button_9_out), .out_5(_4_BIT_MOD_out_5), .in_4(RESET), .in_2(start_stop_1_out_3));  // open: in_1
  ALU alu_1 (
    .in_1(out_29), .RAM(out_29), .out_8(out_13), .out_9(out_29), .out_10(out_15), .B(out_29),
    .MDR(MDR_out_5), .E(ALU_E), .in_2(A_E), .in_5(ALU_L));
  START_STOP start_stop_1 (.in_1(button_10_out), .in_2(or_1_out), .out_3(start_stop_1_out_3));
  or or_1 (or_1_out, button_11_out, STOP);
  Button button_10 (.out(button_10_out));
  Button button_11 (.out(button_11_out));

  // Notes on the sheet:
  //   ROM
  //   contents of rom_1 (hex, n*v repeats v):
  //   d00 9200 2400 102000 200000 408800 40 9*0 d00 9200 2400 102000 200000 800800 804000 40 8*0 d00 9200
  //   2400 102000 200000 800000 20008800 400000 40 7*0 d00 9200 2400 102000 200000 40000 21800 4100 2080
  //   40 6*0 d00 9200 2400 102000 200000 2080 40 9*0 d00 9200 2400 102000 200000 2 40 9*0 d00 9200 2400
  //   102000 200000 6 40 409*0 d00 9200 2400 102000 200000 800000 802000 2002000 12002000 20002000
  //   20402000 40 40 0 0 0 d00 9200 2400 102000 200000 800000 802000 2002000 12002000 20002000 20402000 40
  //   40 0 0 0 d00 9200 2400 102000 200000 800000 802000 2002000 12002000 20002000 20402000 40 40 0 0 0
  //   d00 9200 2400 102000 200000 800000 802000 2002000 12002000 20002000 20402000 40 40 0 0 0 d00 9200
  //   2400 102000 200000 2000000 2400000 40 8*0 d00 9200 2400 102000 200000 800000 1800000 40 8*0 d00 9200
  //   2400 102000 200000 40000 20c00 404000 40 7*0 d00 9200 2400 102000 200000 20c00 408000 80000 40 7*0
  //   d00 9200 2400 102000 200000 20c00 8080 80000 40 7*0 d00 9200 2400 102000 200000 40002000 80400000 40
  //   8*0 d00 9200 2400 102000 200040 11*0 d00 9200 2400 102000 200000 802000 c0802000 80402000 40 7*0 d00
  //   9200 2400 102000 200000 802000 c0802000 402000 40 7*0 d00 9200 2400 102000 200000 802000 c0802000
  //   402000 40 7*0 d00 9200 2400 102000 200000 802000 c0802000 402000 40 7*0 d00 9200 2400 102000 200000
  //   0 20 9*0 d00 9200 2400 102000 200000 4402000 40 9*0 d00 9200 2400 102000 200000 8802000 40
  //   RAM
  //   DATA LINE CONTENT
  //   CLICK ME
  //   FOR
  //   CLOCK PULSE
  //   START
  //   /RESTART
  //   RESET
endmodule

module reg_8bit (
  input  [7:0] in_1,
  input  L,
  input  in_3,
  output [7:0] out_4
);

  wire [7:0] register_1_q, register_2_q;

  Register #(.trigger("high")) register_1 (.D(in_1), .en(1'b1), .Q(register_1_q), .clk(L), .clr(1'b0));
  Register register_2 (.D(register_1_q), .en(1'b1), .Q(register_2_q), .clk(in_3), .clr(1'b0));
  assign out_4 = in_3 ? register_2_q : 8'bz;  // Controlled_Buffer controlled_buffer_1
endmodule

module reg_12bit (
  input  [11:0] in_1,
  input  L,
  input  E,
  output [11:0] out_4,
  output [11:0] out_5
);

  wire [11:0] register_2_q;

  Register #(.width(12), .trigger("high")) register_1 (.D(in_1), .en(1'b1), .Q(out_4), .clk(L), .clr(1'b0));
  Register #(.width(12)) register_2 (.D(out_4), .en(1'b1), .Q(register_2_q), .clk(E), .clr(1'b0));
  assign out_5 = E ? register_2_q : 12'bz;  // Controlled_Buffer controlled_buffer_1
endmodule

module PC (
  input  I,
  input  [7:0] in_2,
  input  in_3,
  input  in_4,
  input  in_5,
  output [7:0] out_6
);

  wire or_1_out, or_2_out;
  wire [7:0] adder_1_out, controlled_buffer_1_out, reg_8bit_1_out_4;

  or or_1 (or_1_out, I, in_5, in_4);
  assign controlled_buffer_1_out = in_5 ? {8{1'b0}} : 8'bz;  // Controlled_Buffer controlled_buffer_1
  Multiplexer #(.width(8)) multiplexer_1 (
    .in0(adder_1_out), .in1(in_2), .out(controlled_buffer_1_out), .sel(in_4), .en(1'b1));
  or or_2 (or_2_out, I, in_3);
  reg_8bit reg_8bit_1 (.in_1(controlled_buffer_1_out), .L(or_1_out), .out_4(reg_8bit_1_out_4), .in_3(or_2_out));
  Adder adder_1 (.a({{7{1'b0}}, I}), .b(reg_8bit_1_out_4), .out(adder_1_out));  // open: cin, cout
  assign out_6 = in_3 ? reg_8bit_1_out_4 : 8'bz;  // Controlled_Buffer controlled_buffer_2
endmodule

module SP (
  input  D,
  input  I,
  input  [7:0] in_3,
  input  START,
  input  L,
  input  E,
  output [7:0] out_7
);

  wire and_1_out, not_1_out, or_1_out, or_2_out;
  wire [7:0] adder_1_out, controlled_buffer_1_out, multiplexer_1_out, reg_8bit_1_out_4, subtractor_1_out;

  assign controlled_buffer_1_out = START ? {8{1'b1}} : 8'bz;  // Controlled_Buffer controlled_buffer_1
  and and_1 (and_1_out, D, not_1_out);
  Multiplexer #(.width(8)) multiplexer_1 (
    .in0(adder_1_out), .in1(subtractor_1_out), .out(multiplexer_1_out), .sel(and_1_out), .en(1'b1));
  or or_1 (or_1_out, I, START, D, L);
  not not_1 (not_1_out, I);
  Multiplexer #(.width(8)) multiplexer_2 (
    .in0(multiplexer_1_out), .in1(in_3), .out(controlled_buffer_1_out), .sel(L), .en(1'b1));
  or or_2 (or_2_out, I, D, E);
  reg_8bit reg_8bit_1 (.in_1(controlled_buffer_1_out), .L(or_1_out), .out_4(reg_8bit_1_out_4), .in_3(or_2_out));
  Adder adder_1 (.a({{7{1'b0}}, I}), .b(reg_8bit_1_out_4), .out(adder_1_out));  // open: cin, cout
  assign out_7 = E ? reg_8bit_1_out_4 : 8'bz;  // Controlled_Buffer controlled_buffer_2
  Subtractor subtractor_1 (.a(reg_8bit_1_out_4), .b({{7{1'b0}}, D}), .out(subtractor_1_out));  // open: bin, bout
endmodule

module RAM (
  input  [7:0] in_1,
  input  [7:0] in_2,
  input  in_3,
  input  in_4,
  output [11:0] out_5
);

  wire [11:0] rom_1_data;

  ROM #(.dataWidth(12)) rom_1 (.addr(in_2), .data(rom_1_data), .sel(1'b1));
  RAM_part #(.dataWidth(12), .bus("separate")) ram_1 (
    .addr(in_1), .data(out_5), .str(in_3), .sel(1'b1), .clk(in_3), .ld(in_4), .clr(1'b0));  // open: din
endmodule

module DECODING (
  input  [11:0] MDR,
  output [5:0] IR,
  output [3:0] out_3
);

  and and_1 (IR[4], MDR[11], IR[5]);
  Multiplexer #(.width(4), .enable("false")) multiplexer_1 (
    .in0(MDR[11:8]), .in1(MDR[7:4]), .out(IR[3:0]), .sel(IR[5]));
  and and_2 (IR[5], MDR[10], MDR[9], MDR[8]);

  assign out_3 = MDR[3:0];

  // Notes on the sheet:
  //   IR: pull=down
  //   MDR: pull=up
  //   I
  //   M
endmodule

module MOD_COUNTER (
  input  [3:0] in_1,
  input  in_2,
  input  in_3,
  input  in_4,
  output [3:0] out_5
);

  Counter #(.width(4), .max('hf)) counter_1 (
    .load(1'b0), .D(in_1), .count(in_2), .Q(out_5), .clk(in_3), .clr(in_4));  // open: carry
endmodule

module ALU (
  input  [11:0] in_1,
  input  in_2,
  input  [11:0] RAM,
  input  [11:0] B,
  input  in_5,
  input  E,
  input  [11:0] MDR,
  output out_8,
  output [11:0] out_9,
  output out_10
);

  wire adder_1_cout, and_1_out, multiplexer_3_out, nor_1_out, not_2_out, subtractor_1_bout;
  wire [1:0] multiplexer_2_out;
  wire [11:0] adder_1_out, multiplexer_1_out, multiplexer_4_out, not_1_out, register_1_q, register_2_q,
       subtractor_1_out;

  Multiplexer #(.width(12), .disabled(0), .enable("false")) multiplexer_1 (
    .in0(RAM), .in1(B), .out(multiplexer_1_out), .sel(and_1_out));
  and and_1 (and_1_out, MDR[10], MDR[9], MDR[8]);
  Register #(.width(12), .trigger("high")) register_1 (.D(in_1), .en(1'b1), .Q(register_1_q), .clk(in_2), .clr(1'b0));
  Register #(.width(12), .trigger("high")) register_2 (
    .D(multiplexer_1_out), .en(1'b1), .Q(register_2_q), .clk(in_5), .clr(1'b0));
  Adder #(.width(12)) adder_1 (.a(register_1_q), .b(register_2_q), .out(adder_1_out), .cin(1'b0), .cout(adder_1_cout));
  Subtractor #(.width(12)) subtractor_1 (
    .a(register_1_q), .b(register_2_q), .out(subtractor_1_out), .bin(1'b0), .bout(subtractor_1_bout));
  assign not_1_out = ~register_1_q;  // NOT_Gate not_1, 12 bits wide
  Multiplexer #(.width(2), .disabled(0), .enable("false")) multiplexer_2 (
    .in0(2'b00), .in1(MDR[5:4]), .out(multiplexer_2_out), .sel(and_1_out));
  Multiplexer #(.disabled(0), .enable("false")) multiplexer_3 (
    .in0(adder_1_cout), .in1(not_2_out), .out(multiplexer_3_out), .sel(multiplexer_2_out[0]));
  not not_2 (not_2_out, subtractor_1_bout);
  Multiplexer #(.select(2), .width(12), .enable("false")) multiplexer_4 (
    .in0(adder_1_out), .in1(subtractor_1_out), .in2({12{1'b0}}), .in3(not_1_out), .out(multiplexer_4_out),
    .sel(multiplexer_2_out));
  assign out_9 = E ? multiplexer_4_out : 12'bz;  // Controlled_Buffer controlled_buffer_1
  Register #(.width(1), .trigger("high")) register_3 (.D(multiplexer_3_out), .en(1'b1), .Q(out_8), .clk(E), .clr(1'b0));
  nor nor_1 (nor_1_out, multiplexer_4_out[0], multiplexer_4_out[1], multiplexer_4_out[2], multiplexer_4_out[3], multiplexer_4_out[4], multiplexer_4_out[5], multiplexer_4_out[6], multiplexer_4_out[7], multiplexer_4_out[8], multiplexer_4_out[9], multiplexer_4_out[10], multiplexer_4_out[11]);
  Register #(.width(1), .trigger("high")) register_4 (.D(nor_1_out), .en(1'b1), .Q(out_10), .clk(E), .clr(1'b0));
endmodule

module SHIFTER (
  input  [11:0] in_1,
  input  in_2,
  input  [11:0] in_3,
  input  in_4,
  output [11:0] out_5
);

  wire and_1_out, and_2_out, and_3_out, and_4_out, and_5_out, decoder_1_out1, decoder_1_out3, decoder_1_out5,
       decoder_1_out6, not_1_out;
  wire [11:0] register_1_q, shifter_1_out, shifter_2_out, shifter_3_out, shifter_4_out;

  not not_1 (not_1_out, in_3[11]);
  and and_1 (and_1_out, not_1_out, in_3[10], in_3[9], in_3[8], in_3[7]);
  Decoder #(.select(3), .disabled(0)) decoder_1 (
    .out1(decoder_1_out1), .out3(decoder_1_out3), .out5(decoder_1_out5), .out6(decoder_1_out6),
    .sel({in_3[4], in_3[5], in_3[6]}), .en(and_1_out));  // open: out0, out2, out4, out7
  Register #(.width(12), .trigger("high")) register_1 (.D(in_1), .en(1'b1), .Q(register_1_q), .clk(in_2), .clr(1'b0));
  Shifter #(.width(12)) shifter_1 (.in(register_1_q), .\dist (in_3[3:0]), .out(shifter_1_out));
  and and_2 (and_2_out, decoder_1_out6, in_4);
  Shifter #(.width(12), .shift("lr")) shifter_2 (.in(register_1_q), .\dist (in_3[3:0]), .out(shifter_2_out));
  and and_3 (and_3_out, decoder_1_out1, in_4);
  Shifter #(.width(12), .shift("ar")) shifter_3 (.in(register_1_q), .\dist (in_3[3:0]), .out(shifter_3_out));
  and and_4 (and_4_out, decoder_1_out3, in_4);
  Shifter #(.width(12), .shift("rr")) shifter_4 (.in(register_1_q), .\dist (in_3[3:0]), .out(shifter_4_out));
  and and_5 (and_5_out, decoder_1_out5, in_4);
  assign out_5 = and_2_out ? shifter_1_out : 12'bz;  // Controlled_Buffer controlled_buffer_1
  assign out_5 = and_3_out ? shifter_2_out : 12'bz;  // Controlled_Buffer controlled_buffer_2
  assign out_5 = and_4_out ? shifter_3_out : 12'bz;  // Controlled_Buffer controlled_buffer_3
  assign out_5 = and_5_out ? shifter_4_out : 12'bz;  // Controlled_Buffer controlled_buffer_4

  // Notes on the sheet:
  //   LSC
  //   RSC
  //   ASR
  //   RRX
endmodule

module reg_4bit (
  input  L,
  input  [3:0] in_2,
  output [3:0] out_3
);

  wire [3:0] undriven;

  Register #(.width(4), .trigger("high")) register_1 (.D(undriven), .en(1'b1), .Q(out_3), .clk(L), .clr(1'b0));
endmodule

module IN_PORT (
  input  [11:0] in_1,
  input  in_2,
  input  [11:0] in_3,
  input  in_4,
  input  [11:0] in_5,
  input  [11:0] in_6,
  input  in_7,
  input  [3:0] in_8,
  input  in_9,
  input  in_10,
  output [11:0] out_11,
  output [3:0] out_12
);

  wire decoder_1_out1, decoder_1_out2, decoder_1_out4, decoder_1_out8;

  Register #(.width(1), .trigger("high")) register_1 (
    .D(in_2), .en(1'b1), .Q(out_12[0]), .clk(in_2), .clr(decoder_1_out1));
  Register #(.width(1), .trigger("high")) register_2 (
    .D(in_4), .en(1'b1), .Q(out_12[1]), .clk(in_4), .clr(decoder_1_out2));
  Decoder #(.select(4), .disabled(0)) decoder_1 (
    .out1(decoder_1_out1), .out2(decoder_1_out2), .out4(decoder_1_out4), .out8(decoder_1_out8), .sel(in_8),
    .en(in_7));  // open: out0, out3, out5, out6, out7, out9, out10, out11, out12, out13, out14, out15
  Register #(.width(1), .trigger("high")) register_3 (
    .D(in_9), .en(1'b1), .Q(out_12[2]), .clk(in_9), .clr(decoder_1_out4));
  Register #(.width(1), .trigger("high")) register_4 (
    .D(in_10), .en(1'b1), .Q(out_12[3]), .clk(in_10), .clr(decoder_1_out8));
  reg_12bit reg_12bit_1 (.in_1(in_1), .L(in_2), .E(decoder_1_out1), .out_5(out_11));  // open: out_4
  reg_12bit reg_12bit_2 (.in_1(in_3), .L(in_4), .E(decoder_1_out2), .out_5(out_11));  // open: out_4
  reg_12bit reg_12bit_3 (.in_1(in_5), .L(in_9), .E(decoder_1_out4), .out_5(out_11));  // open: out_4
  reg_12bit reg_12bit_4 (.in_1(in_6), .L(in_10), .E(decoder_1_out8), .out_5(out_11));  // open: out_4
endmodule

module OUT_PORT (
  input  [11:0] in_1,
  input  in_2,
  input  in_3,
  input  in_4,
  input  [3:0] in_5,
  input  in_6,
  input  in_7,
  output [11:0] out_8,
  output [11:0] out_9,
  output [3:0] out_10,
  output [11:0] out_11,
  output [11:0] out_12
);

  wire decoder_1_out1, decoder_1_out2, decoder_1_out4, decoder_1_out8;

  Register #(.width(1), .trigger("high")) register_1 (
    .D(in_2), .en(1'b1), .Q(out_10[0]), .clk(in_2), .clr(decoder_1_out1));
  Register #(.width(1), .trigger("high")) register_2 (
    .D(in_3), .en(1'b1), .Q(out_10[1]), .clk(in_3), .clr(decoder_1_out2));
  Decoder #(.select(4), .disabled(0)) decoder_1 (
    .out1(decoder_1_out1), .out2(decoder_1_out2), .out4(decoder_1_out4), .out8(decoder_1_out8), .sel(in_5),
    .en(in_4));  // open: out0, out3, out5, out6, out7, out9, out10, out11, out12, out13, out14, out15
  Register #(.width(1), .trigger("high")) register_3 (
    .D(in_6), .en(1'b1), .Q(out_10[2]), .clk(in_6), .clr(decoder_1_out4));
  Register #(.width(1), .trigger("high")) register_4 (
    .D(in_7), .en(1'b1), .Q(out_10[3]), .clk(in_7), .clr(decoder_1_out8));
  reg_12bit reg_12bit_1 (.in_1(in_1), .L(decoder_1_out1), .E(in_2), .out_5(out_8));  // open: out_4
  reg_12bit reg_12bit_2 (.in_1(in_1), .L(decoder_1_out2), .E(in_3), .out_5(out_9));  // open: out_4
  reg_12bit reg_12bit_3 (.in_1(in_1), .L(decoder_1_out4), .E(in_6), .out_5(out_11));  // open: out_4
  reg_12bit reg_12bit_4 (.in_1(in_1), .L(decoder_1_out8), .E(in_7), .out_5(out_12));  // open: out_4
endmodule

module CONTROL_SECTION (
  input  [11:0] in_1,
  output BS_E,
  output BS_L,
  output ALU_E,
  output ALU_L,
  output OUT_L,
  output IN_E,
  output B_E,
  output B_L,
  output A_E,
  output A_L,
  output IR_E,
  output IR_L,
  output SP_I,
  output SP_D,
  output SP_E,
  output SP_L,
  output RAM_E,
  output RAM_L,
  output MDR_E,
  output MDR_L,
  output MAR_E,
  output MAR_L,
  output PC_I,
  output PC_E,
  output PC_L,
  output out_27,
  output STOP,
  output START
);

  ROM #(.addrWidth(12), .dataWidth(28)) rom_1 (
    .addr(in_1),
    .data({BS_E, BS_L, ALU_E, ALU_L, OUT_L, IN_E, B_E, B_L, A_E, A_L, IR_E, IR_L, SP_I, SP_D, SP_E, SP_L, RAM_E, RAM_L, MDR_E, MDR_L, MAR_E, MAR_L, PC_I, PC_E, PC_L, out_27, STOP, START}),
    .sel(1'b1));
endmodule

module START_STOP (
  input  in_1,
  input  in_2,
  output out_3
);

  Register #(.width(1)) register_1 (.D(1'b1), .en(1'b1), .Q(out_3), .clk(in_1), .clr(in_2));
endmodule

module CND (
  input  in_1,
  input  in_2,
  input  in_3,
  input  in_4,
  input  in_5,
  output out_6
);

  Multiplexer #(.select(2)) multiplexer_1 (
    .in0(in_1), .in1(in_2), .in2(1'b1), .in3(1'b0), .out(out_6), .sel({in_3, in_4}), .en(in_5));
endmodule

module IR (
  input  [7:0] in_1,
  input  in_2,
  input  in_3,
  output [7:0] out_4
);

  Register register_1 (.D(in_1), .en(1'b1), .Q(out_4), .clk(in_2), .clr(in_3));
endmodule

module IR_REG (
  input  [7:0] in_1,
  input  in_2,
  input  in_3,
  input  in_4,
  output [7:0] out_5
);

  wire [7:0] register_1_q;

  Register register_1 (.D(in_1), .en(1'b1), .Q(register_1_q), .clk(in_2), .clr(1'b0));
  Register register_2 (.D(register_1_q), .en(1'b1), .Q(out_5), .clk(in_4), .clr(in_3));
endmodule

module MAR (
  input  [7:0] in_1,
  input  in_2,
  input  in_3,
  output [7:0] out_4
);

  wire [7:0] controlled_buffer_1_out, register_1_q;

  Register #(.trigger("high")) register_1 (.D(in_1), .en(1'b1), .Q(register_1_q), .clk(in_2), .clr(1'b0));
  assign controlled_buffer_1_out = in_3 ? register_1_q : 8'bz;  // Controlled_Buffer controlled_buffer_1
  Register #(.trigger("high")) register_2 (.D(controlled_buffer_1_out), .en(1'b1), .Q(out_4), .clk(in_3), .clr(1'b0));
endmodule
